# Fritzing sketch schema (saved by Fritzing 0.9.3b)

parts:
  WeMos_D1_Mini1 = WeMos D1 Mini
  Součástka1 = HX711 Weighing Sensor Module
  S1 = Load Sensor - 50kg [part_number=SEN-10245]
  S2 = Load Sensor - 50kg [part_number=SEN-10245]
  S3 = Load Sensor - 50kg [part_number=SEN-10245]
  S4 = Load Sensor - 50kg [part_number=SEN-10245]

nets:
  5V: WeMos_D1_Mini1.5V, Součástka1.VCC
  N1: WeMos_D1_Mini1.D0, WeMos_D1_Mini1.RST
  N2: WeMos_D1_Mini1.D1, Součástka1.CK/TX
  N3: WeMos_D1_Mini1.D2, Součástka1.DO/RX
  N4: WeMos_D1_Mini1.G, Součástka1.GND
  N5: Součástka1.E+, S4.R
  N6: Součástka1.E-, S1.R
  N7: Součástka1.A+, S3.R
  N8: Součástka1.A-, S2.R
  N9: S1.B, S2.B
  N10: S1.W, S3.W
  N11: S2.W, S4.W
  N12: S3.B, S4.B

notes:
  Pohled na váhu zezadu (zespoda)
  Důležitá je barva drátů.
  E+ | white
  E- || green
  A- ||| green
  A+ |||| white
  Pozor, neodpovídá zelenému boardu HX711

custom parts:
  Load Sensor - 50kg: Half-wheatstone bridge Load Cell modified from the Fritzing Repo This load sensor, sometimes called a strain gauge, is the same one found in digital bathroom scales (you know, the ones you use in January for your New Year's resolutions, and then forget about a month later). This sensor can measure up to about 110 pounds.
